// Logisim project LC3-2200a.circ as structural Verilog: 4 circuits, main circuit Datapath
module Datapath (
);

  wire and_1_out, and_2_out, and_3_out, and_4_out, CLK, comparator_2_lt, DrALU, DrMEM, DrOFF, DrPC, DrREG,
       EnInt, IE, IntAck, IntOut, LdA, LdB, LdCC, LdEnInt, LdIR, LdMAR, LdPC, N, or_1_out, P, WrMEM, WrREG, Z;
  wire [1:0] func;
  wire [2:0] comparator_1_gt;
  wire [3:0] regno;
  wire [23:0] register_4_q;
  wire [31:0] alu_1_out_4, bit_extender_1_out, controlled_buffer_1_out, intergenerator_1_deviceid, IR,
       multiplexer_1_out, PC_q, ram_1_data, ram_2_data, register_1_q, register_2_q;
  wire [31:24] register_4_q_2;

  Clock clock_1 (.out(CLK));
  Register #(.width(32)) PC (.D(controlled_buffer_1_out), .en(LdPC), .Q(PC_q), .clk(CLK));  // open: clr
  Multiplexer #(.width(32), .disabled(0), .enable("false")) multiplexer_1 (
    .in0(PC_q), .in1(32'h10), .out(multiplexer_1_out), .sel(comparator_2_lt));
  assign controlled_buffer_1_out = DrPC ? multiplexer_1_out : 32'bz;  // Controlled_Buffer controlled_buffer_1
  Comparator #(.width(32), .mode("unsigned")) comparator_1 (
    .a(controlled_buffer_1_out), .b({32{1'b0}}), .gt(comparator_1_gt[0]), .eq(comparator_1_gt[1]),
    .lt(comparator_1_gt[2]));
  and and_1 (and_1_out, IR[22], N);
  and and_2 (and_2_out, IR[21], Z);
  or or_1 (or_1_out, and_1_out, and_2_out, and_3_out);
  Intergenerator intergenerator_1 (.CLK(CLK), .IntAck(IntAck), .IntOut(IntOut), .DeviceID(intergenerator_1_deviceid));
  assign controlled_buffer_1_out = IntAck ? intergenerator_1_deviceid : 32'bz;  // Controlled_Buffer controlled_buffer_2
  Comparator #(.width(32), .mode("unsigned")) comparator_2 (
    .a(PC_q), .b(32'h10), .lt(comparator_2_lt));  // open: gt, eq
  Register #(.width(3)) CC (.D(comparator_1_gt), .en(LdCC), .Q({N, Z, P}), .clk(CLK));  // open: clr
  and and_3 (and_3_out, IR[20], P);
  Register #(.width(32)) register_1 (.D(controlled_buffer_1_out), .en(LdA), .Q(register_1_q), .clk(CLK));  // open: clr
  ALU alu_1 (.A(register_1_q), .B(register_2_q), .func(func), .out_4(alu_1_out_4));
  assign controlled_buffer_1_out = DrALU ? alu_1_out_4 : 32'bz;  // Controlled_Buffer controlled_buffer_3
  Register #(.width(32)) register_2 (.D(controlled_buffer_1_out), .en(LdB), .Q(register_2_q), .clk(CLK));  // open: clr
  Register #(.width(1)) register_3 (.D(EnInt), .en(LdEnInt), .Q(IE), .clk(CLK));  // open: clr
  and and_4 (and_4_out, IE, IntOut);
  RAM #(.addrWidth(4), .dataWidth(32), .bus("separate")) ram_1 (
    .addr(regno), .din(controlled_buffer_1_out), .data(ram_1_data), .str(WrREG), .clk(CLK));  // open: sel, ld, clr
  assign controlled_buffer_1_out = DrREG ? ram_1_data : 32'bz;  // Controlled_Buffer controlled_buffer_4
  Control_Unit control_unit_1 (
    .CCMatch(or_1_out), .IR(IR), .DrREG(DrREG), .DrMEM(DrMEM), .DrALU(DrALU), .DrPC(DrPC), .DrOFF(DrOFF),
    .LdPC(LdPC), .LdIR(LdIR), .LdMAR(LdMAR), .LdA(LdA), .LdB(LdB), .LdCC(LdCC), .WrREG(WrREG), .WrMEM(WrMEM),
    .ALU(func), .regno(regno), .CLK(CLK), .LdEnInt(LdEnInt), .EnInt(EnInt), .IntAck(IntAck),
    .Inputs(and_4_out));
  Register #(.width(32)) register_4 (
    .D(controlled_buffer_1_out), .en(LdMAR), .Q({register_4_q_2, register_4_q}), .clk(CLK));  // open: clr
  RAM #(.addrWidth(24), .dataWidth(32), .bus("separate")) ram_2 (
    .addr(register_4_q), .din(controlled_buffer_1_out), .data(ram_2_data), .str(WrMEM), .clk(CLK));  // open: sel, ld, clr
  assign controlled_buffer_1_out = DrMEM ? ram_2_data : 32'bz;  // Controlled_Buffer controlled_buffer_5
  Register #(.width(32)) u_IR (.D(controlled_buffer_1_out), .en(LdIR), .Q(IR), .clk(CLK));  // open: clr
  assign controlled_buffer_1_out = DrOFF ? bit_extender_1_out : 32'bz;  // Controlled_Buffer controlled_buffer_6
  assign bit_extender_1_out = {{12{IR[19]}}, IR[19:0]};  // Bit_Extender bit_extender_1

  // Other names for the same wires on the sheet: p_t = IR[20]; z_t = IR[21]; n_t = IR[22]

  // Notes on the sheet:
  //   CheckCC
endmodule

// ALU:32
module ALU (
  input  [31:0] A,
  input  [31:0] B,
  input  [1:0] func,
  output [31:0] out_4
);

  wire [31:0] adder_1_out, adder_2_out, nand_1_out;

  Adder #(.width(32)) adder_1 (.a(A), .b(B), .out(adder_1_out));  // open: cin, cout
  assign nand_1_out = ~(A & B);  // NAND_Gate nand_1, 32 bits wide
  Multiplexer #(.select(2), .width(32), .disabled(0), .enable("false")) multiplexer_1 (
    .in0(adder_1_out), .in1(nand_1_out), .in2(adder_2_out), .out(out_4), .sel(func));  // open: in3
  Adder #(.width(32)) adder_2 (.a(A), .b(32'h1), .out(adder_2_out));  // open: cin, cout

  // Notes on the sheet:
  //   The 32-bit ALU
endmodule

module Control_Unit (
  input  CCMatch,
  input  Inputs,
  input  [31:0] IR,
  input  CLK,
  output DrREG,
  output DrMEM,
  output DrALU,
  output DrPC,
  output DrOFF,
  output LdPC,
  output LdIR,
  output LdMAR,
  output LdA,
  output LdB,
  output LdCC,
  output WrREG,
  output WrMEM,
  output EnInt,
  output [1:0] ALU,
  output IntAck,
  output LdEnInt,
  output [3:0] regno
);

  wire chkCC, OPTest, or_1_out;
  wire [1:0] RegSel;
  wire [5:0] multiplexer_1_out, rom_1_data, rom_2_data, rom_3_data, rom_4_data, State_q;
  wire [17:17] rom_2_data_2;

  Register #(.width(6)) State (.D(multiplexer_1_out), .en(1'b1), .Q(State_q), .clk(CLK));  // open: clr
  ROM #(.addrWidth(2), .dataWidth(6)) rom_1 (.addr({1'b0, Inputs}), .data(rom_1_data));  // open: sel
  ROM #(.addrWidth(6), .dataWidth(28)) rom_2 (
    .addr(State_q),
    .data({IntAck, EnInt, LdEnInt, chkCC, OPTest, ALU, RegSel, WrMEM, rom_2_data_2[17], LdCC, LdB, LdA, LdMAR, LdIR, LdPC, DrOFF, DrPC, DrALU, DrMEM, DrREG, rom_2_data}));  // open: sel
  Multiplexer #(.select(2), .width(6), .disabled(0), .enable("false")) multiplexer_1 (
    .in0(rom_2_data), .in1(rom_3_data), .in2(rom_4_data), .in3(rom_1_data), .out(multiplexer_1_out),
    .sel({chkCC, OPTest}));
  ROM #(.addrWidth(4), .dataWidth(6)) rom_3 (.addr(IR[31:28]), .data(rom_3_data));  // open: sel
  ROM #(.addrWidth(2), .dataWidth(6)) rom_4 (.addr({1'b0, CCMatch}), .data(rom_4_data));  // open: sel
  or or_1 (or_1_out, regno[0], regno[1], regno[2], regno[3]);
  Multiplexer #(.select(2), .width(4), .disabled(0), .enable("false")) multiplexer_2 (
    .in0(IR[27:24]), .in1(IR[23:20]), .in2(IR[3:0]), .in3(4'b1100), .out(regno), .sel(RegSel));
  and and_1 (WrREG, or_1_out, rom_2_data_2[17]);

  // Other names for the same wires on the sheet: onInt = Inputs

  // Notes on the sheet:
  //   Primary State ROM
  //   contents of rom_1 (hex, n*v repeats v):
  //   0 25
  //   contents of rom_2 (hex, n*v repeats v):
  //   6201 1082 c00900 84044 108045 30124 84047 8408 30124 8404a 10804b 230124 1000000 420e 840f 924 20211
  //   80864 84053 8414 2115 300a4 4217 8418 30124 8405a 841b 211c 40064 8405e 841f 630124 20 6000024
  //   2000000 6180864 1800000 1a0226 2000027 8002028 880
  //   IR[15..13] ROM
  //   CCMatch ROM
  //   contents of rom_3 (hex, n*v repeats v):
  //   3 6 9 c 10 12 16 19 21 22 23 4*0 20
  //   contents of rom_4 (hex, n*v repeats v):
  //   0 d
  //   Outputs
  //   Zero Reigster Write Lock
endmodule

module Intergenerator (
  input  CLK,
  input  IntAck,
  output IntOut,
  output [31:0] DeviceID
);

  wire comparator_1_eq;
  wire [9:0] adder_1_out, register_1_q;

  Adder #(.width(10)) adder_1 (.a(10'h1), .b(register_1_q), .out(adder_1_out));  // open: cin, cout
  Register #(.width(10)) register_1 (.D(adder_1_out), .en(1'b1), .Q(register_1_q), .clk(CLK));  // open: clr
  Comparator #(.width(10), .mode("unsigned")) comparator_1 (
    .a({10{1'b1}}), .b(register_1_q), .eq(comparator_1_eq));  // open: gt, lt
  Register #(.width(1)) register_2 (.D(comparator_1_eq), .en(comparator_1_eq), .Q(IntOut), .clk(CLK), .clr(IntAck));

  assign DeviceID = 32'h1;
endmodule
